// Logisim project RISC-V Datapath.circ as structural Verilog: 14 circuits, main circuit main
module main (
  input  Clock,
  input  in_2,
  input  Enable
);

  wire control_unit_1_alusrc, control_unit_1_memread, control_unit_1_memtoreg, control_unit_1_memwrite,
       control_unit_1_regwrite;
  wire [3:0] alu_control_1_aluoperation;
  wire [8:0] control_unit_1_out_2;
  wire [23:0] bit_extender_1_out;
  wire [31:0] alu_1_out_4, data_memory_1_out_6, imm_gen_1_out_2, multiplexer_1_out, multiplexer_2_out,
       ram_1_out_3, register_file_1_read_data1, register_file_1_read_data2;

  // Probe on ram_1_out_3
  RAM ram_1 (.clock(Clock), .enable(Enable), .out_3(ram_1_out_3));
  // Probe on ram_1_out_3[11:7]
  Imm_Gen imm_gen_1 (.in_1(ram_1_out_3), .out_2(imm_gen_1_out_2));
  Control_Unit control_unit_1 (
    .Opcode(ram_1_out_3[6:0]), .MemRead(control_unit_1_memread), .MemtoReg(control_unit_1_memtoreg),
    .MemWrite(control_unit_1_memwrite), .ALUSrc(control_unit_1_alusrc), .RegWrite(control_unit_1_regwrite),
    .out_2(control_unit_1_out_2[0]), .out_3(control_unit_1_out_2[1]), .out_4(control_unit_1_out_2[2]),
    .out_5(control_unit_1_out_2[3]), .out_6(control_unit_1_out_2[4]), .out_7(control_unit_1_out_2[5]),
    .out_8(control_unit_1_out_2[6]), .out_9(control_unit_1_out_2[7]), .out_10(control_unit_1_out_2[8]));  // open: Branch
  Register_File register_file_1 (
    .write_data(multiplexer_2_out), .Clock(Clock), .WriteReg(control_unit_1_regwrite),
    .Write_reg(ram_1_out_3[11:7]), .Read_Reg1(ram_1_out_3[19:15]), .Read_Reg2(ram_1_out_3[24:20]),
    .Reset(in_2), .Read_data1(register_file_1_read_data1), .Read_data2(register_file_1_read_data2));
  Multiplexer #(.width(32)) multiplexer_1 (
    .in0(register_file_1_read_data2), .in1(imm_gen_1_out_2), .out(multiplexer_1_out),
    .sel(control_unit_1_alusrc));  // open: en
  // Probe on register_file_1_read_data1
  // Probe on multiplexer_1_out
  ALU_Control alu_control_1 (
    .func7(ram_1_out_3[31:25]), .func3(ram_1_out_3[14:12]), .ALUop(control_unit_1_out_2),
    .ALUOperation(alu_control_1_aluoperation));
  // Probe on alu_control_1_aluoperation
  ALU alu_1 (
    .in_1(register_file_1_read_data1), .in_2(multiplexer_1_out), .in_3(alu_control_1_aluoperation),
    .out_4(alu_1_out_4));
  Bit_Extender #(.in_width(32), .out_width(24)) bit_extender_1 (.in(alu_1_out_4), .out(bit_extender_1_out));
  Data_Memory data_memory_1 (
    .in_1(bit_extender_1_out), .in_2(register_file_1_read_data2), .Memwrite(control_unit_1_memwrite),
    .clock(Clock), .MemRead(control_unit_1_memread), .out_6(data_memory_1_out_6));
  // Probe on alu_1_out_4
  // Probe on multiplexer_2_out
  Multiplexer #(.width(32)) multiplexer_2 (
    .in0(alu_1_out_4), .in1(data_memory_1_out_6), .out(multiplexer_2_out), .sel(control_unit_1_memtoreg));  // open: en
endmodule

module full_adder (
  input  b,
  input  a,
  input  cin,
  output cout,
  output sum
);

  wire and_1_out, and_2_out, xor_1_out;

  and and_1 (and_1_out, b, a);
  or or_1 (cout, and_1_out, and_2_out);
  and and_2 (and_2_out, cin, xor_1_out);
  xor xor_1 (xor_1_out, b, a);
  xor xor_2 (sum, cin, xor_1_out);
endmodule

module _4_bit_parallel_adder (
  input  [3:0] in_1,
  input  [3:0] in_2,
  input  in_3,
  output [3:0] out_4,
  output out_5
);

  wire full_adder_2_cout, full_adder_3_cout, full_adder_4_cout;

  full_adder full_adder_1 (.b(in_1[3]), .a(in_2[3]), .cout(out_5), .sum(out_4[3]), .cin(full_adder_2_cout));
  full_adder full_adder_2 (.b(in_1[2]), .a(in_2[2]), .cout(full_adder_2_cout), .sum(out_4[2]), .cin(full_adder_3_cout));
  full_adder full_adder_3 (.b(in_1[1]), .a(in_2[1]), .cout(full_adder_3_cout), .sum(out_4[1]), .cin(full_adder_4_cout));
  full_adder full_adder_4 (.b(in_1[0]), .a(in_2[0]), .cout(full_adder_4_cout), .sum(out_4[0]), .cin(in_3));
endmodule

module _32_bit_full_adder (
  input  [31:0] in_1,
  input  [31:0] in_2,
  input  Cin,
  output [31:0] out_4,
  output out_5
);

  wire n4_bit_parallel_adder_2_out_5, n4_bit_parallel_adder_3_out_5, n4_bit_parallel_adder_4_out_5,
       n4_bit_parallel_adder_5_out_5, n4_bit_parallel_adder_6_out_5, n4_bit_parallel_adder_7_out_5,
       n4_bit_parallel_adder_8_out_5;

  _4_bit_parallel_adder u_4_bit_parallel_adder_1 (
    .in_1(in_2[31:28]), .in_2(in_1[31:28]), .out_5(out_5), .out_4(out_4[31:28]),
    .in_3(n4_bit_parallel_adder_2_out_5));
  _4_bit_parallel_adder u_4_bit_parallel_adder_2 (
    .in_1(in_2[27:24]), .in_2(in_1[27:24]), .out_5(n4_bit_parallel_adder_2_out_5), .out_4(out_4[27:24]),
    .in_3(n4_bit_parallel_adder_3_out_5));
  _4_bit_parallel_adder u_4_bit_parallel_adder_3 (
    .in_1(in_2[23:20]), .in_2(in_1[23:20]), .out_5(n4_bit_parallel_adder_3_out_5), .out_4(out_4[23:20]),
    .in_3(n4_bit_parallel_adder_4_out_5));
  _4_bit_parallel_adder u_4_bit_parallel_adder_4 (
    .in_1(in_2[19:16]), .in_2(in_1[19:16]), .out_5(n4_bit_parallel_adder_4_out_5), .out_4(out_4[19:16]),
    .in_3(n4_bit_parallel_adder_5_out_5));
  _4_bit_parallel_adder u_4_bit_parallel_adder_5 (
    .in_1(in_2[15:12]), .in_2(in_1[15:12]), .out_5(n4_bit_parallel_adder_5_out_5), .out_4(out_4[15:12]),
    .in_3(n4_bit_parallel_adder_6_out_5));
  _4_bit_parallel_adder u_4_bit_parallel_adder_6 (
    .in_1(in_2[11:8]), .in_2(in_1[11:8]), .out_5(n4_bit_parallel_adder_6_out_5), .out_4(out_4[11:8]),
    .in_3(n4_bit_parallel_adder_7_out_5));
  _4_bit_parallel_adder u_4_bit_parallel_adder_7 (
    .in_1(in_2[7:4]), .in_2(in_1[7:4]), .out_5(n4_bit_parallel_adder_7_out_5), .out_4(out_4[7:4]),
    .in_3(n4_bit_parallel_adder_8_out_5));
  _4_bit_parallel_adder u_4_bit_parallel_adder_8 (
    .in_1(in_2[3:0]), .in_2(in_1[3:0]), .out_5(n4_bit_parallel_adder_8_out_5), .out_4(out_4[3:0]), .in_3(Cin));
endmodule

module full_substractor (
  input  b,
  input  a,
  input  Bin,
  output Bout,
  output D
);

  wire and_1_out, and_2_out, not_1_out, not_2_out, xor_1_out;

  and and_1 (and_1_out, b, not_1_out);
  or or_1 (Bout, and_1_out, and_2_out);
  not not_1 (not_1_out, a);
  not not_2 (not_2_out, xor_1_out);
  and and_2 (and_2_out, Bin, not_2_out);
  xor xor_1 (xor_1_out, b, a);
  xor xor_2 (D, Bin, xor_1_out);
endmodule

module _4_bit_parallel_sub (
  input  [3:0] in_1,
  input  [3:0] in_2,
  input  in_3,
  output out_4,
  output [3:0] out_5
);

  wire full_substractor_2_bout, full_substractor_3_bout, full_substractor_4_bout;

  full_substractor full_substractor_1 (
    .b(in_1[3]), .a(in_2[3]), .Bout(out_4), .D(out_5[3]), .Bin(full_substractor_2_bout));
  full_substractor full_substractor_2 (
    .b(in_1[2]), .a(in_2[2]), .Bout(full_substractor_2_bout), .D(out_5[2]), .Bin(full_substractor_3_bout));
  full_substractor full_substractor_3 (
    .b(in_1[1]), .a(in_2[1]), .Bout(full_substractor_3_bout), .D(out_5[1]), .Bin(full_substractor_4_bout));
  full_substractor full_substractor_4 (
    .b(in_1[0]), .a(in_2[0]), .Bout(full_substractor_4_bout), .D(out_5[0]), .Bin(in_3));
endmodule

module _32_bit_full_sub (
  input  [31:0] in_1,
  input  [31:0] in_2,
  input  in_3,
  output [31:0] out_4,
  output out_5
);

  wire n4_bit_parallel_sub_2_out_4, n4_bit_parallel_sub_3_out_4, n4_bit_parallel_sub_4_out_4,
       n4_bit_parallel_sub_5_out_4, n4_bit_parallel_sub_6_out_4, n4_bit_parallel_sub_7_out_4,
       n4_bit_parallel_sub_8_out_4;

  _4_bit_parallel_sub u_4_bit_parallel_sub_1 (
    .in_1(in_2[31:28]), .in_2(in_1[31:28]), .out_4(out_5), .out_5(out_4[31:28]),
    .in_3(n4_bit_parallel_sub_2_out_4));
  _4_bit_parallel_sub u_4_bit_parallel_sub_2 (
    .in_1(in_2[27:24]), .in_2(in_1[27:24]), .out_4(n4_bit_parallel_sub_2_out_4), .out_5(out_4[27:24]),
    .in_3(n4_bit_parallel_sub_3_out_4));
  _4_bit_parallel_sub u_4_bit_parallel_sub_3 (
    .in_1(in_2[23:20]), .in_2(in_1[23:20]), .out_4(n4_bit_parallel_sub_3_out_4), .out_5(out_4[23:20]),
    .in_3(n4_bit_parallel_sub_4_out_4));
  _4_bit_parallel_sub u_4_bit_parallel_sub_4 (
    .in_1(in_2[19:16]), .in_2(in_1[19:16]), .out_4(n4_bit_parallel_sub_4_out_4), .out_5(out_4[19:16]),
    .in_3(n4_bit_parallel_sub_5_out_4));
  _4_bit_parallel_sub u_4_bit_parallel_sub_5 (
    .in_1(in_2[15:12]), .in_2(in_1[15:12]), .out_4(n4_bit_parallel_sub_5_out_4), .out_5(out_4[15:12]),
    .in_3(n4_bit_parallel_sub_6_out_4));
  _4_bit_parallel_sub u_4_bit_parallel_sub_6 (
    .in_1(in_2[11:8]), .in_2(in_1[11:8]), .out_4(n4_bit_parallel_sub_6_out_4), .out_5(out_4[11:8]),
    .in_3(n4_bit_parallel_sub_7_out_4));
  _4_bit_parallel_sub u_4_bit_parallel_sub_7 (
    .in_1(in_2[7:4]), .in_2(in_1[7:4]), .out_4(n4_bit_parallel_sub_7_out_4), .out_5(out_4[7:4]),
    .in_3(n4_bit_parallel_sub_8_out_4));
  _4_bit_parallel_sub u_4_bit_parallel_sub_8 (
    .in_1(in_2[3:0]), .in_2(in_1[3:0]), .out_4(n4_bit_parallel_sub_8_out_4), .out_5(out_4[3:0]), .in_3(in_3));
endmodule

module Control_Unit (
  input  [6:0] Opcode,
  output out_2,
  output out_3,
  output out_4,
  output out_5,
  output out_6,
  output out_7,
  output out_8,
  output out_9,
  output out_10,
  output Branch,
  output MemRead,
  output MemtoReg,
  output MemWrite,
  output ALUSrc,
  output RegWrite
);

  wire not_1_out, not_2_out, op4_out, op5_out, op6_out;

  not op5 (op5_out, Opcode[5]);
  not op6 (op6_out, Opcode[6]);
  not op4 (op4_out, Opcode[4]);
  not not_1 (not_1_out, Opcode[3]);
  not not_2 (not_2_out, Opcode[2]);
  and R_type (out_2, not_2_out, not_1_out, Opcode[4], Opcode[5], op6_out);
  and I_type (out_3, not_2_out, not_1_out, Opcode[4], op5_out, op6_out);
  and L_type (MemRead, not_2_out, not_1_out, op4_out, op5_out, op6_out);
  and S_type (MemWrite, not_2_out, not_1_out, op4_out, Opcode[5], op6_out);
  and B_type (Branch, not_2_out, not_1_out, op4_out, Opcode[5], Opcode[6]);
  and jal (out_7, Opcode[2], Opcode[3], op4_out, Opcode[5], Opcode[6]);
  and jalr (out_8, Opcode[2], not_1_out, op4_out, Opcode[5], Opcode[6]);
  and lui (out_9, Opcode[2], not_1_out, Opcode[4], Opcode[5], op6_out);
  and auipc (out_10, Opcode[2], not_1_out, Opcode[4], op5_out, op6_out);
  or or_1 (ALUSrc, out_3, MemRead, MemWrite, out_8, out_9);
  or or_2 (RegWrite, out_2, out_3, MemRead, out_7, out_8, out_9);

  assign MemtoReg = MemRead;
  assign out_4 = MemRead;
  assign out_5 = MemWrite;
  assign out_6 = Branch;

  // Notes on the sheet:
  //   op3
  //   op0
  //   op1
  //   op2
endmodule

module ALU_Control (
  input  [6:0] func7,
  input  [2:0] func3,
  input  [8:0] ALUop,
  output [3:0] ALUOperation
);

  wire _000_out, _001_out, _010_out, _011_out, _100_out, _101_out, _110_out, _111_out, ADD_out, AND_out,
       BEQ_out, BGE_out, BGEU_out, BNE_out, not_1_out, not_2_out, not_3_out, not_4_out, or_1_out, or_2_out,
       or_3_out, or_4_out, or_5_out, OR_6_out, SLL_out, SLT_BLT_out, SLTU_out, SRA_out, SRL_out, SUB_out,
       XOR_out;

  not not_1 (not_1_out, func7[5]);
  not not_2 (not_2_out, func3[1]);
  not not_3 (not_3_out, func3[2]);
  not not_4 (not_4_out, func3[0]);
  and _110 (_110_out, func3[2], func3[1], not_4_out);
  and _111 (_111_out, func3[2], func3[1], func3[0]);
  and _100 (_100_out, func3[2], not_2_out, not_4_out);
  and _000 (_000_out, not_3_out, not_2_out, not_4_out);
  and _101 (_101_out, func3[2], not_2_out, func3[0]);
  and _001 (_001_out, not_3_out, not_2_out, func3[0]);
  and _011 (_011_out, not_3_out, func3[1], func3[0]);
  and _010 (_010_out, not_3_out, func3[1], not_4_out);
  or or_1 (or_1_out, ALUop[0], ALUop[1]);
  or or_2 (or_2_out, or_1_out, _001_out);
  or or_3 (or_3_out, _100_out, _010_out);
  or or_4 (or_4_out, or_1_out, ALUop[2], ALUop[3], ALUop[6], ALUop[7], ALUop[8]);
  or or_5 (or_5_out, _000_out, _010_out);
  and OR_6 (OR_6_out, or_1_out, _110_out);
  and AND (AND_out, or_1_out, _111_out);
  and XOR (XOR_out, or_1_out, _100_out);
  and SUB (SUB_out, func7[5], ALUop[0], _000_out);
  and BGE (BGE_out, ALUop[4], _101_out);
  and BEQ (BEQ_out, ALUop[4], _000_out);
  and BNE (BNE_out, ALUop[4], _001_out);
  and BGEU (BGEU_out, ALUop[4], _111_out);
  and SLTU (SLTU_out, or_1_out, _011_out);
  and SRL (SRL_out, or_1_out, not_1_out, _101_out);
  and SRA (SRA_out, or_1_out, func7[5], _101_out);
  and SLL (SLL_out, or_1_out, _001_out);
  and SLT_BLT (SLT_BLT_out, or_2_out, or_3_out);
  and ADD (ADD_out, or_4_out, or_5_out);
  Priority_Encoder #(.select(4)) priority_encoder_1 (
    .in0(OR_6_out), .in1(AND_out), .in2(ADD_out), .in3(SUB_out), .in4(BGE_out), .in5(SLT_BLT_out),
    .in6(BEQ_out), .in7(BNE_out), .in8(SLL_out), .in9(XOR_out), .in10(SRL_out), .in11(SRA_out),
    .in12(BGEU_out), .in13(SLTU_out), .out(ALUOperation));  // open: in14, in15, gs, en_out, en_in
endmodule

module ALU (
  input  [31:0] in_1,
  input  [31:0] in_2,
  input  [3:0] in_3,
  output [31:0] out_4
);

  wire comparator_1_eq, comparator_1_lt, comparator_2_lt, not_1_out, not_2_out, not_3_out;
  wire [31:0] and_1_out, bit_extender_1_out, bit_extender_2_out, bit_extender_3_out, bit_extender_4_out,
       bit_extender_5_out, bit_extender_6_out, n32_bit_full_adder_1_out_4, n32_bit_full_sub_1_out_4,
       or_1_out, shifter_1_out, shifter_2_out, shifter_3_out, xor_1_out;

  assign or_1_out = in_1 | in_2;  // OR_Gate or_1, 32 bits wide
  assign and_1_out = in_1 & in_2;  // AND_Gate and_1, 32 bits wide
  _32_bit_full_adder u_32_bit_full_adder_1 (
    .in_1(in_1), .in_2(in_2), .Cin(1'b0), .out_4(n32_bit_full_adder_1_out_4));  // open: out_5
  _32_bit_full_sub u_32_bit_full_sub_1 (
    .in_1(in_1), .in_2(in_2), .in_3(1'b0), .out_4(n32_bit_full_sub_1_out_4));  // open: out_5
  Comparator #(.width(32)) comparator_1 (.a(in_1), .b(in_2), .eq(comparator_1_eq), .lt(comparator_1_lt));  // open: gt
  Shifter #(.width(32)) shifter_1 (.in(in_1), .\dist (in_2[4:0]), .out(shifter_1_out));
  assign xor_1_out = in_1 ^ in_2;  // XOR_Gate xor_1, 32 bits wide
  Shifter #(.width(32), .shift("lr")) shifter_2 (.in(in_1), .\dist (in_2[4:0]), .out(shifter_2_out));
  Shifter #(.width(32), .shift("ar")) shifter_3 (.in(in_1), .\dist (in_2[4:0]), .out(shifter_3_out));
  Comparator #(.width(32), .mode("unsigned")) comparator_2 (.a(in_1), .b(in_2), .lt(comparator_2_lt));  // open: gt, eq
  not not_1 (not_1_out, comparator_1_lt);
  not not_2 (not_2_out, comparator_2_lt);
  assign bit_extender_1_out = {{31{1'b0}}, not_1_out};  // Bit_Extender bit_extender_1
  not not_3 (not_3_out, comparator_1_eq);
  assign bit_extender_2_out = {{31{1'b0}}, not_2_out};  // Bit_Extender bit_extender_2
  assign bit_extender_3_out = {{31{1'b0}}, comparator_2_lt};  // Bit_Extender bit_extender_3
  assign bit_extender_4_out = {{31{1'b0}}, comparator_1_lt};  // Bit_Extender bit_extender_4
  assign bit_extender_5_out = {{31{1'b0}}, comparator_1_eq};  // Bit_Extender bit_extender_5
  assign bit_extender_6_out = {{31{1'b0}}, not_3_out};  // Bit_Extender bit_extender_6
  Multiplexer #(.select(4), .width(32)) multiplexer_1 (
    .in0(or_1_out), .in1(and_1_out), .in2(n32_bit_full_adder_1_out_4), .in3(n32_bit_full_sub_1_out_4),
    .in4(bit_extender_1_out), .in5(bit_extender_4_out), .in6(bit_extender_5_out), .in7(bit_extender_6_out),
    .in8(shifter_1_out), .in9(xor_1_out), .in10(shifter_2_out), .in11(shifter_3_out),
    .in12(bit_extender_2_out), .in13(bit_extender_3_out), .out(out_4), .sel(in_3));  // open: in14, in15, en
endmodule

module Register_File (
  input  [31:0] write_data,
  input  [4:0] Read_Reg1,
  input  [4:0] Read_Reg2,
  input  Clock,
  input  Reset,
  input  WriteReg,
  input  [4:0] Write_reg,
  output [31:0] Read_data1,
  output [31:0] Read_data2
);

  wire and_1_out, and_2_out, and_3_out, and_4_out, and_5_out, and_6_out, and_7_out, and_8_out, and_9_out,
       and_10_out, and_11_out, and_12_out, and_13_out, and_14_out, and_15_out, and_16_out, and_17_out,
       and_18_out, and_19_out, and_20_out, and_21_out, and_22_out, and_23_out, and_24_out, and_25_out,
       and_26_out, and_27_out, and_28_out, and_29_out, and_30_out, and_31_out, and_32_out, decoder_1_out0,
       decoder_1_out1, decoder_1_out2, decoder_1_out3, decoder_1_out4, decoder_1_out5, decoder_1_out6,
       decoder_1_out7, decoder_1_out8, decoder_1_out9, decoder_1_out10, decoder_1_out11, decoder_1_out12,
       decoder_1_out13, decoder_1_out14, decoder_1_out15, decoder_1_out16, decoder_1_out17, decoder_1_out18,
       decoder_1_out19, decoder_1_out20, decoder_1_out21, decoder_1_out22, decoder_1_out23, decoder_1_out24,
       decoder_1_out25, decoder_1_out26, decoder_1_out27, decoder_1_out28, decoder_1_out29, decoder_1_out30,
       decoder_1_out31;
  wire [31:0] _0_q, _1_q, _2_q, _3_q, _4_q, _5_q, _6_q, _7_q, _8_q, _9_q, _10_q, _11_q, _12_q, _13_q, _14_q,
       _15_q, _16_q, _17_q, _18_q, _19_q, _20_q, _21_q, _22_q, _23_q, _24_q, _25_q, _26_q, _27_q, _28_q,
       _29_q, _30_q, _31_q;

  Decoder #(.select(5)) decoder_1 (
    .out0(decoder_1_out0), .out1(decoder_1_out1), .out2(decoder_1_out2), .out3(decoder_1_out3),
    .out4(decoder_1_out4), .out5(decoder_1_out5), .out6(decoder_1_out6), .out7(decoder_1_out7),
    .out8(decoder_1_out8), .out9(decoder_1_out9), .out10(decoder_1_out10), .out11(decoder_1_out11),
    .out12(decoder_1_out12), .out13(decoder_1_out13), .out14(decoder_1_out14), .out15(decoder_1_out15),
    .out16(decoder_1_out16), .out17(decoder_1_out17), .out18(decoder_1_out18), .out19(decoder_1_out19),
    .out20(decoder_1_out20), .out21(decoder_1_out21), .out22(decoder_1_out22), .out23(decoder_1_out23),
    .out24(decoder_1_out24), .out25(decoder_1_out25), .out26(decoder_1_out26), .out27(decoder_1_out27),
    .out28(decoder_1_out28), .out29(decoder_1_out29), .out30(decoder_1_out30), .out31(decoder_1_out31),
    .sel(Write_reg));  // open: en
  and and_1 (and_1_out, decoder_1_out0, WriteReg);
  and and_2 (and_2_out, decoder_1_out1, WriteReg);
  and and_3 (and_3_out, decoder_1_out2, WriteReg);
  and and_4 (and_4_out, decoder_1_out3, WriteReg);
  and and_5 (and_5_out, decoder_1_out4, WriteReg);
  and and_6 (and_6_out, decoder_1_out5, WriteReg);
  and and_7 (and_7_out, decoder_1_out6, WriteReg);
  and and_8 (and_8_out, decoder_1_out7, WriteReg);
  and and_9 (and_9_out, decoder_1_out8, WriteReg);
  and and_10 (and_10_out, decoder_1_out9, WriteReg);
  and and_11 (and_11_out, decoder_1_out10, WriteReg);
  and and_12 (and_12_out, decoder_1_out11, WriteReg);
  and and_13 (and_13_out, decoder_1_out12, WriteReg);
  and and_14 (and_14_out, decoder_1_out13, WriteReg);
  and and_15 (and_15_out, decoder_1_out14, WriteReg);
  and and_16 (and_16_out, decoder_1_out15, WriteReg);
  and and_17 (and_17_out, decoder_1_out16, WriteReg);
  and and_18 (and_18_out, decoder_1_out17, WriteReg);
  and and_19 (and_19_out, decoder_1_out18, WriteReg);
  and and_20 (and_20_out, decoder_1_out19, WriteReg);
  and and_21 (and_21_out, decoder_1_out20, WriteReg);
  and and_22 (and_22_out, decoder_1_out21, WriteReg);
  and and_23 (and_23_out, decoder_1_out22, WriteReg);
  and and_24 (and_24_out, decoder_1_out23, WriteReg);
  and and_25 (and_25_out, decoder_1_out24, WriteReg);
  and and_26 (and_26_out, decoder_1_out25, WriteReg);
  and and_27 (and_27_out, decoder_1_out26, WriteReg);
  and and_28 (and_28_out, decoder_1_out27, WriteReg);
  and and_29 (and_29_out, decoder_1_out28, WriteReg);
  and and_30 (and_30_out, decoder_1_out29, WriteReg);
  and and_31 (and_31_out, decoder_1_out30, WriteReg);
  and and_32 (and_32_out, decoder_1_out31, WriteReg);
  Register #(.width(32)) _0 (.D(write_data), .en(and_1_out), .Q(_0_q), .clk(Clock), .clr(Reset));
  Register #(.width(32)) _1 (.D(write_data), .en(and_2_out), .Q(_1_q), .clk(Clock), .clr(Reset));
  Register #(.width(32)) _2 (.D(write_data), .en(and_3_out), .Q(_2_q), .clk(Clock), .clr(Reset));
  Register #(.width(32)) _3 (.D(write_data), .en(and_4_out), .Q(_3_q), .clk(Clock), .clr(Reset));
  Register #(.width(32)) _4 (.D(write_data), .en(and_5_out), .Q(_4_q), .clk(Clock), .clr(Reset));
  Register #(.width(32)) _5 (.D(write_data), .en(and_6_out), .Q(_5_q), .clk(Clock), .clr(Reset));
  Register #(.width(32)) _6 (.D(write_data), .en(and_7_out), .Q(_6_q), .clk(Clock), .clr(Reset));
  Register #(.width(32)) _7 (.D(write_data), .en(and_8_out), .Q(_7_q), .clk(Clock), .clr(Reset));
  Register #(.width(32)) _8 (.D(write_data), .en(and_9_out), .Q(_8_q), .clk(Clock), .clr(Reset));
  Register #(.width(32)) _9 (.D(write_data), .en(and_10_out), .Q(_9_q), .clk(Clock), .clr(Reset));
  Register #(.width(32)) _10 (.D(write_data), .en(and_11_out), .Q(_10_q), .clk(Clock), .clr(Reset));
  Register #(.width(32)) _11 (.D(write_data), .en(and_12_out), .Q(_11_q), .clk(Clock), .clr(Reset));
  Register #(.width(32)) _12 (.D(write_data), .en(and_13_out), .Q(_12_q), .clk(Clock), .clr(Reset));
  Register #(.width(32)) _13 (.D(write_data), .en(and_14_out), .Q(_13_q), .clk(Clock), .clr(Reset));
  Register #(.width(32)) _14 (.D(write_data), .en(and_15_out), .Q(_14_q), .clk(Clock), .clr(Reset));
  Register #(.width(32)) _15 (.D(write_data), .en(and_16_out), .Q(_15_q), .clk(Clock), .clr(Reset));
  Register #(.width(32)) _16 (.D(write_data), .en(and_17_out), .Q(_16_q), .clk(Clock), .clr(Reset));
  Register #(.width(32)) _17 (.D(write_data), .en(and_18_out), .Q(_17_q), .clk(Clock), .clr(Reset));
  Register #(.width(32)) _18 (.D(write_data), .en(and_19_out), .Q(_18_q), .clk(Clock), .clr(Reset));
  Register #(.width(32)) _19 (.D(write_data), .en(and_20_out), .Q(_19_q), .clr(Reset));  // open: clk
  Register #(.width(32)) _20 (.D(write_data), .en(and_21_out), .Q(_20_q), .clr(Reset));  // open: clk
  Register #(.width(32)) _21 (.D(write_data), .en(and_22_out), .Q(_21_q), .clr(Reset));  // open: clk
  Register #(.width(32)) _22 (.D(write_data), .en(and_23_out), .Q(_22_q), .clr(Reset));  // open: clk
  Register #(.width(32)) _23 (.D(write_data), .en(and_24_out), .Q(_23_q), .clr(Reset));  // open: clk
  Register #(.width(32)) _24 (.D(write_data), .en(and_25_out), .Q(_24_q), .clk(Clock), .clr(Reset));
  Register #(.width(32)) _25 (.D(write_data), .en(and_26_out), .Q(_25_q), .clr(Reset));  // open: clk
  Register #(.width(32)) _26 (.D(write_data), .en(and_27_out), .Q(_26_q), .clr(Reset));  // open: clk
  Register #(.width(32)) _27 (.D(write_data), .en(and_28_out), .Q(_27_q), .clk(Clock), .clr(Reset));
  Register #(.width(32)) _28 (.en(and_29_out), .Q(_28_q), .clk(Clock), .clr(Reset));  // open: D
  Register #(.width(32)) _29 (.en(and_30_out), .Q(_29_q), .clk(Clock), .clr(Reset));  // open: D
  Register #(.width(32)) _30 (.en(and_31_out), .Q(_30_q), .clk(Clock), .clr(Reset));  // open: D
  Register #(.width(32)) _31 (.en(and_32_out), .Q(_31_q), .clk(Clock), .clr(Reset));  // open: D
  Multiplexer #(.select(5), .width(32)) multiplexer_1 (
    .in0(_0_q), .in1(_1_q), .in2(_2_q), .in3(_3_q), .in4(_4_q), .in5(_5_q), .in6(_6_q), .in7(_7_q),
    .in8(_8_q), .in9(_9_q), .in10(_10_q), .in11(_11_q), .in12(_12_q), .in13(_13_q), .in14(_14_q),
    .in15(_15_q), .in16(_16_q), .in17(_17_q), .in18(_18_q), .in19(_19_q), .in20(_20_q), .in21(_21_q),
    .in22(_22_q), .in23(_23_q), .in24(_24_q), .in25(_25_q), .in26(_26_q), .in27(_27_q), .in28(_28_q),
    .in29(_29_q), .in30(_30_q), .in31(_31_q), .out(Read_data1), .sel(Read_Reg1));  // open: en
  Multiplexer #(.select(5), .width(32)) multiplexer_2 (
    .in0(_0_q), .in1(_1_q), .in2(_2_q), .in3(_3_q), .in4(_4_q), .in5(_5_q), .in6(_6_q), .in7(_7_q),
    .in8(_8_q), .in9(_9_q), .in10(_10_q), .in11(_11_q), .in12(_12_q), .in13(_13_q), .in14(_14_q),
    .in15(_15_q), .in16(_16_q), .in17(_17_q), .in18(_18_q), .in19(_19_q), .in20(_20_q), .in21(_21_q),
    .in22(_22_q), .in23(_23_q), .in24(_24_q), .in25(_25_q), .in26(_26_q), .in27(_27_q), .in28(_28_q),
    .in29(_29_q), .in30(_30_q), .in31(_31_q), .out(Read_data2), .sel(Read_Reg2));  // open: en
endmodule

module Imm_Gen (
  input  [31:0] in_1,
  output [31:0] out_2
);

  wire not_1_out;
  wire [0:0] undriven, undriven_2;
  wire [1:0] and_1_out;
  wire [11:0] undriven_3;
  wire [31:0] bit_extender_1_out, bit_extender_2_out, bit_extender_3_out, bit_extender_4_out,
       bit_extender_5_out;

  not not_1 (not_1_out, in_1[2]);
  and and_1 (and_1_out[0], in_1[5], not_1_out);
  xor xor_1 (and_1_out[1], in_1[2], in_1[6]);
  assign bit_extender_1_out = {{20{1'b0}}, in_1[31:20]};  // Bit_Extender bit_extender_1
  assign bit_extender_2_out = {{20{1'b0}}, {in_1[31:25], in_1[11:7]}};  // Bit_Extender bit_extender_2
  assign bit_extender_3_out = {{11{1'b0}}, {in_1[31], in_1[19:12], in_1[20], in_1[30:21], undriven[0]}};  // Bit_Extender bit_extender_3
  assign bit_extender_4_out = {{19{1'b0}}, {in_1[31], in_1[7], in_1[30:25], in_1[11:8], undriven_2[0]}};  // Bit_Extender bit_extender_4
  Bit_Extender #(.in_width(32), .out_width(32)) bit_extender_5 (
    .in({in_1[31:12], undriven_3}), .out(bit_extender_5_out));
  Multiplexer #(.select(3), .width(32)) multiplexer_1 (
    .in0(bit_extender_1_out), .in1(bit_extender_2_out), .in2(bit_extender_3_out), .in3(bit_extender_4_out),
    .in4(bit_extender_5_out), .out(out_2), .sel({in_1[3], and_1_out}));  // open: in5, in6, in7, en

  // Notes on the sheet:
  //   I-Type
  //   S-Type
  //   J-Type
  //   B-Type
  //   U-Type
endmodule

module RAM (
  input  clock,
  input  enable,
  output [31:0] out_3
);

  wire [23:0] adder_1_out;
  wire [31:0] register_1_q;
  wire [31:24] adder_1_out_2;

  RAM_part #(.addrWidth(24), .dataWidth(32)) ram_1 (
    .addr(adder_1_out), .data(out_3), .clk(clock), .ld(enable));  // open: sel, clr
  Register #(.width(32)) register_1 (.D({adder_1_out_2, adder_1_out}), .Q(register_1_q), .clk(clock));  // open: en, clr
  Adder #(.width(32)) adder_1 (.a(register_1_q), .b(32'h1), .out({adder_1_out_2, adder_1_out}));  // open: cin, cout
endmodule

module Data_Memory (
  input  [23:0] in_1,
  input  [31:0] in_2,
  input  Memwrite,
  input  clock,
  input  MemRead,
  output [31:0] out_6
);

  RAM_part #(.addrWidth(24), .dataWidth(32), .bus("separate")) ram_1 (
    .addr(in_1), .din(in_2), .data(out_6), .sel(Memwrite), .clk(clock), .ld(MemRead));  // open: str, clr
endmodule
